# Fritzing sketch Pfad-Findr (saved by Fritzing 0.9.3b)
breadboards: 1
stripboards: 1

parts:
  LED1 = RGB LED (com. anode, rbg) [package="5 mm [THT]"]
  LED2 = RGB LED (com. anode, rbg) [package="5 mm [THT]"]
  LED3 = RGB LED (com. anode, rbg) [package="5 mm [THT]"]
  LED4 = RGB LED (com. anode, rbg) [package="5 mm [THT]"]
  Part1 = Arduino Ethernet Shield (Rev3)

nets:
  N1: LED1.red_cathode, Part1.SPI/D13
  N2: LED1.common_anode, LED1.green_cathode, LED2.common_anode, LED2.green_cathode, LED3.common_anode, LED3.green_cathode, LED4.common_anode, LED4.green_cathode, Part1.GND
  N3: LED2.red_cathode, Part1.SPI/D12
  N4: LED3.red_cathode, Part1.PWM_D11
  N5: LED4.red_cathode, Part1.ETH_CS
